# Fritzing sketch module_alarm_keypad (saved by Fritzing 0.7.12b)
perfboards: 1

parts:
  LED2 = yellow LED - 5mm [package="5 mm [THT]"]
  LED3 = LED - 3mm [color="Red (633nm)" package="3 mm [THT]"]
  R2 = 3.3k Ω Resistor [package=THT]
  Arduino1 = Arduino
  R4 = 3.3k Ω Resistor [package=THT]
  J1 = Piezo Speaker

nets:
  N1: LED2.cathode, R4.Pin_0
  N2: LED2.anode, Arduino1.D11
  N3: LED3.cathode, R2.Pin_1
  N4: LED3.anode, Arduino1.D12
  N5: R2.Pin_0, Arduino1.GND, R4.Pin_1, J1.pin1
  N6: Arduino1.D10, J1.pin2
